// Logisim project marie-architecture.circ as structural Verilog: 6 circuits, main circuit main
module main (
  input  [15:0] DebugInput,
  input  [15:0] DebugAddress,
  input  R,
  input  in_4,
  input  Debug_Reset,
  output E
);

  wire Clock_out, controlunit_1_ac_clear_signal, controlunit_1_ac_load_signal, controlunit_1_ar_clear_signal,
       controlunit_1_ar_load_signal, controlunit_1_dr_load_signal, controlunit_1_ir_load_signal,
       controlunit_1_pc_inc_signal, controlunit_1_pc_load_signal, controlunit_1_ram_write_signal,
       controlunit_1_sc_clear_signal, decoder_1_out0, decoder_1_out1, decoder_1_out2, decoder_1_out3,
       decoder_1_out4, decoder_1_out5, decoder_1_out6, decoder_1_out7, decoder_2_out0, decoder_2_out1,
       decoder_2_out2, decoder_2_out3, decoder_2_out4, decoder_2_out5, decoder_2_out6, decoder_2_out7,
       decoder_2_out8, decoder_2_out9, decoder_2_out10, decoder_2_out11, decoder_2_out12, decoder_2_out13,
       decoder_2_out14, decoder_2_out15, or_1_out;
  wire [0:0] controlunit_1_alu_signals;
  wire [2:0] controlunit_1_alu_signals_2, controlunit_1_bus_select_lines;
  wire [3:0] bit_extender_5_out, counter_1_q, n12hexsplitter_1__0, n12hexsplitter_1__1, n12hexsplitter_1__2,
       n12hexsplitter_2__0, n12hexsplitter_2__1, n12hexsplitter_2__2, n16hexsplitter_1__0,
       n16hexsplitter_1__1, n16hexsplitter_1__2, n16hexsplitter_1__3, n16hexsplitter_2__0,
       n16hexsplitter_2__1, n16hexsplitter_2__2, n16hexsplitter_2__3, n16hexsplitter_3__0,
       n16hexsplitter_3__1, n16hexsplitter_3__2, n16hexsplitter_3__3, n16hexsplitter_4__0,
       n16hexsplitter_4__1, n16hexsplitter_4__2, n16hexsplitter_4__3, n16hexsplitter_5__0,
       n16hexsplitter_5__1, n16hexsplitter_5__2, n16hexsplitter_5__3, n16hexsplitter_6__0,
       n16hexsplitter_6__1, n16hexsplitter_6__2, n16hexsplitter_6__3;
  wire [11:0] AR_q, bit_extender_1_out, bit_extender_2_out, multiplexer_1_out, n12bitincrementer_1_output,
       PC_q;
  wire [15:0] AC_q, alu_1_output, bit_extender_3_out, bit_extender_4_out, DR_q, IR_q, multiplexer_2_out,
       ram_1_data, TR_q;

  Counter #(.width(4), .max('hf)) counter_1 (
    .Q(counter_1_q), .clk(Clock_out), .clr(or_1_out));  // open: load, D, count, carry
  or or_1 (or_1_out, controlunit_1_sc_clear_signal, Debug_Reset);
  Decoder #(.select(3)) decoder_1 (
    .out0(decoder_1_out0), .out1(decoder_1_out1), .out2(decoder_1_out2), .out3(decoder_1_out3),
    .out4(decoder_1_out4), .out5(decoder_1_out5), .out6(decoder_1_out6), .out7(decoder_1_out7),
    .sel(IR_q[14:12]));  // open: en
  Decoder #(.select(4)) decoder_2 (
    .out0(decoder_2_out0), .out1(decoder_2_out1), .out2(decoder_2_out2), .out3(decoder_2_out3),
    .out4(decoder_2_out4), .out5(decoder_2_out5), .out6(decoder_2_out6), .out7(decoder_2_out7),
    .out8(decoder_2_out8), .out9(decoder_2_out9), .out10(decoder_2_out10), .out11(decoder_2_out11),
    .out12(decoder_2_out12), .out13(decoder_2_out13), .out14(decoder_2_out14), .out15(decoder_2_out15),
    .sel(counter_1_q));  // open: en
  ControlUnit controlunit_1 (
    .Operand__0_11(IR_q[11:0]), .AR_Load_Signal(controlunit_1_ar_load_signal),
    .AR_Clear_Signal(controlunit_1_ar_clear_signal), .SC_Clear_Signal(controlunit_1_sc_clear_signal),
    .AC_Load_Signal(controlunit_1_ac_load_signal), .AC_Clear_Signal(controlunit_1_ac_clear_signal),
    .Bus_Select_Lines(controlunit_1_bus_select_lines), .PC_Load_Signal(controlunit_1_pc_load_signal),
    .RAM_Write_Signal(controlunit_1_ram_write_signal), .IR_Load_Signal(controlunit_1_ir_load_signal),
    .DR_Load_Signal(controlunit_1_dr_load_signal), .R(R), .I(IR_q[15]), .D0(decoder_1_out0),
    .D1(decoder_1_out1), .D2(decoder_1_out2), .D3(decoder_1_out3), .D4(decoder_1_out4), .D5(decoder_1_out5),
    .D6(decoder_1_out6), .D7(decoder_1_out7), .T0(decoder_2_out0), .T1(decoder_2_out1), .T2(decoder_2_out2),
    .T3(decoder_2_out3), .T4(decoder_2_out4), .T5(decoder_2_out5), .T6(decoder_2_out6), .T7(decoder_2_out7),
    .T8(decoder_2_out8), .T9(decoder_2_out9), .T10(decoder_2_out10), .T11(decoder_2_out11),
    .T12(decoder_2_out12), .T13(decoder_2_out13), .T14(decoder_2_out14), .T15(decoder_2_out15),
    .PC_INC_Signal(controlunit_1_pc_inc_signal),
    .ALU_Signals({controlunit_1_alu_signals_2, controlunit_1_alu_signals[0]}));
  alu alu_1 (
    .Cin(controlunit_1_alu_signals[0]), .A(AC_q), .B(DR_q), .Select_Lines(controlunit_1_alu_signals_2),
    .Output(alu_1_output), .Cout(E));
  Bit_Extender #(.in_width(16), .out_width(12)) bit_extender_1 (.in(multiplexer_2_out), .out(bit_extender_1_out));
  Bit_Extender #(.in_width(16), .out_width(12)) bit_extender_2 (.in(multiplexer_2_out), .out(bit_extender_2_out));
  Clock Clock (.out(Clock_out));
  Multiplexer #(.width(12)) multiplexer_1 (
    .in0(bit_extender_2_out), .in1(n12bitincrementer_1_output), .out(multiplexer_1_out),
    .sel(controlunit_1_pc_inc_signal));  // open: en
  _12BitIncrementer u_12bitincrementer_1 (.Input(PC_q), .Output(n12bitincrementer_1_output));
  Hex_Digit_Display hex_digit_display_1 (.value(counter_1_q));  // open: dp
  Register #(.width(12)) AR (
    .D(bit_extender_1_out), .en(controlunit_1_ar_load_signal), .Q(AR_q), .clk(Clock_out),
    .clr(controlunit_1_ar_clear_signal));
  Register #(.width(12)) PC (
    .D(multiplexer_1_out), .en(controlunit_1_pc_load_signal), .Q(PC_q), .clk(Clock_out), .clr(in_4));
  Register #(.width(16)) DR (
    .D(multiplexer_2_out), .en(controlunit_1_dr_load_signal), .Q(DR_q), .clk(Clock_out));  // open: clr
  Register #(.width(16)) AC (
    .D(alu_1_output), .en(controlunit_1_ac_load_signal), .Q(AC_q), .clk(Clock_out),
    .clr(controlunit_1_ac_clear_signal));
  Register #(.width(16)) IR (
    .D(multiplexer_2_out), .en(controlunit_1_ir_load_signal), .Q(IR_q), .clk(Clock_out));  // open: clr
  Register #(.width(16)) TR (.D(multiplexer_2_out), .Q(TR_q), .clk(Clock_out));  // open: en, clr
  RAM #(.addrWidth(12), .dataWidth(16), .bus("separate")) ram_1 (
    .addr(AR_q), .din(multiplexer_2_out), .data(ram_1_data), .str(controlunit_1_ram_write_signal),
    .clk(Clock_out));  // open: sel, ld, clr
  Hex_Digit_Display hex_digit_display_2 (.value(n12hexsplitter_1__2));  // open: dp
  _12HexSplitter u_12hexsplitter_1 (
    .in_1(AR_q), ._0(n12hexsplitter_1__0), ._1(n12hexsplitter_1__1), ._2(n12hexsplitter_1__2));
  assign bit_extender_3_out = {{4{1'b0}}, PC_q};  // Bit_Extender bit_extender_3
  Hex_Digit_Display hex_digit_display_3 (.value(n12hexsplitter_2__2));  // open: dp
  _12HexSplitter u_12hexsplitter_2 (
    .in_1(PC_q), ._0(n12hexsplitter_2__0), ._1(n12hexsplitter_2__1), ._2(n12hexsplitter_2__2));
  Hex_Digit_Display hex_digit_display_4 (.value(n16hexsplitter_1__2));  // open: dp
  Hex_Digit_Display hex_digit_display_5 (.value(n16hexsplitter_1__3));  // open: dp
  _16HexSplitter u_16hexsplitter_1 (
    .Input(DR_q), ._0(n16hexsplitter_1__0), ._1(n16hexsplitter_1__1), ._2(n16hexsplitter_1__2),
    ._3(n16hexsplitter_1__3));
  Hex_Digit_Display hex_digit_display_6 (.value(n16hexsplitter_2__3));  // open: dp
  Hex_Digit_Display hex_digit_display_7 (.value(n16hexsplitter_2__2));  // open: dp
  _16HexSplitter u_16hexsplitter_2 (
    .Input(AC_q), ._0(n16hexsplitter_2__0), ._1(n16hexsplitter_2__1), ._2(n16hexsplitter_2__2),
    ._3(n16hexsplitter_2__3));
  Hex_Digit_Display hex_digit_display_8 (.value(n16hexsplitter_3__2));  // open: dp
  Hex_Digit_Display hex_digit_display_9 (.value(n16hexsplitter_3__3));  // open: dp
  _16HexSplitter u_16hexsplitter_3 (
    .Input(IR_q), ._0(n16hexsplitter_3__0), ._1(n16hexsplitter_3__1), ._2(n16hexsplitter_3__2),
    ._3(n16hexsplitter_3__3));
  Hex_Digit_Display hex_digit_display_10 (.value(n16hexsplitter_4__3));  // open: dp
  Hex_Digit_Display hex_digit_display_11 (.value(n16hexsplitter_4__2));  // open: dp
  _16HexSplitter u_16hexsplitter_4 (
    .Input(TR_q), ._0(n16hexsplitter_4__0), ._1(n16hexsplitter_4__1), ._2(n16hexsplitter_4__2),
    ._3(n16hexsplitter_4__3));
  Hex_Digit_Display hex_digit_display_12 (.value(n16hexsplitter_5__3));  // open: dp
  Hex_Digit_Display hex_digit_display_13 (.value(n16hexsplitter_5__2));  // open: dp
  _16HexSplitter u_16hexsplitter_5 (
    .Input(ram_1_data), ._0(n16hexsplitter_5__0), ._1(n16hexsplitter_5__1), ._2(n16hexsplitter_5__2),
    ._3(n16hexsplitter_5__3));
  assign bit_extender_4_out = {{4{1'b0}}, AR_q};  // Bit_Extender bit_extender_4
  Hex_Digit_Display hex_digit_display_14 (.value(n12hexsplitter_1__0));  // open: dp
  Hex_Digit_Display hex_digit_display_15 (.value(n12hexsplitter_1__1));  // open: dp
  Hex_Digit_Display hex_digit_display_16 (.value(n12hexsplitter_2__1));  // open: dp
  Hex_Digit_Display hex_digit_display_17 (.value(n12hexsplitter_2__0));  // open: dp
  Hex_Digit_Display hex_digit_display_18 (.value(n16hexsplitter_1__1));  // open: dp
  Hex_Digit_Display hex_digit_display_19 (.value(n16hexsplitter_1__0));  // open: dp
  Hex_Digit_Display hex_digit_display_20 (.value(n16hexsplitter_2__1));  // open: dp
  Hex_Digit_Display hex_digit_display_21 (.value(n16hexsplitter_2__0));  // open: dp
  Hex_Digit_Display hex_digit_display_22 (.value(n16hexsplitter_3__0));  // open: dp
  Hex_Digit_Display hex_digit_display_23 (.value(n16hexsplitter_3__1));  // open: dp
  Hex_Digit_Display hex_digit_display_24 (.value(n16hexsplitter_4__0));  // open: dp
  Hex_Digit_Display hex_digit_display_25 (.value(n16hexsplitter_4__1));  // open: dp
  Hex_Digit_Display hex_digit_display_26 (.value(n16hexsplitter_5__0));  // open: dp
  Hex_Digit_Display hex_digit_display_27 (.value(n16hexsplitter_5__1));  // open: dp
  Hex_Digit_Display hex_digit_display_28 (.value(n16hexsplitter_6__3));  // open: dp
  _16HexSplitter u_16hexsplitter_6 (
    .Input(multiplexer_2_out), ._0(n16hexsplitter_6__0), ._1(n16hexsplitter_6__1), ._2(n16hexsplitter_6__2),
    ._3(n16hexsplitter_6__3));
  Hex_Digit_Display hex_digit_display_29 (.value(n16hexsplitter_6__2));  // open: dp
  Hex_Digit_Display hex_digit_display_30 (.value(n16hexsplitter_6__1));  // open: dp
  Multiplexer #(.select(3), .width(16)) multiplexer_2 (
    .in1(bit_extender_4_out), .in2(bit_extender_3_out), .in3(DR_q), .in4(AC_q), .in5(IR_q), .in6(TR_q),
    .in7(ram_1_data), .out(multiplexer_2_out), .sel(controlunit_1_bus_select_lines));  // open: in0, en
  Hex_Digit_Display hex_digit_display_31 (.value(bit_extender_5_out));  // open: dp
  assign bit_extender_5_out = {{1{1'b0}}, controlunit_1_bus_select_lines};  // Bit_Extender bit_extender_5
  Hex_Digit_Display hex_digit_display_32 (.value(n16hexsplitter_6__0));  // open: dp

  // Notes on the sheet:
  //   I
  //   OpCode
  //   Connections to Control Unit
  //   Address
  //   ALI AHMED NADEEM - 23017
  //   SC
  //   RAM - 7
  //   AR - 1
  //   PC - 2
  //   DR - 3
  //   AC - 4
  //   IR - 5
  //   TR - 6
  //   BUS
  //   Select Line
endmodule

// ALU
module alu (
  input  Cin,
  input  [15:0] A,
  input  [15:0] B,
  input  [2:0] Select_Lines,
  output [15:0] Output,
  output Cout
);

  wire [15:0] and_1_out, multiplexer_1_out, multiplexer_2_out, not_1_out, not_2_out, not_3_out;

  assign not_1_out = ~A;  // NOT_Gate not_1, 16 bits wide
  assign and_1_out = A & B;  // AND_Gate and_1, 16 bits wide
  Multiplexer #(.select(3), .width(16)) multiplexer_1 (
    .in0(A), .in1(A), .in2(A), .in3(A), .in4({16{1'b0}}), .in5({16{1'b0}}), .in6(not_1_out),
    .out(multiplexer_1_out), .sel(Select_Lines));  // open: in7, en
  assign not_2_out = ~B;  // NOT_Gate not_2, 16 bits wide
  assign not_3_out = ~{16{1'b0}};  // NOT_Gate not_3, 16 bits wide
  Multiplexer #(.select(3), .width(16)) multiplexer_2 (
    .in0(B), .in1(not_2_out), .in2({16{1'b0}}), .in3(not_3_out), .in4(and_1_out), .in5(B), .in6({16{1'b0}}),
    .out(multiplexer_2_out), .sel(Select_Lines));  // open: in7, en
  Adder #(.width(16)) adder_1 (.a(multiplexer_1_out), .b(multiplexer_2_out), .out(Output), .cin(Cin), .cout(Cout));

  // Notes on the sheet:
  //   Minimized ALU for 16 bit microoperations
endmodule

// Control Unit
module ControlUnit (
  input  [11:0] Operand__0_11,
  input  R,
  input  I,
  input  D0,
  input  D1,
  input  D2,
  input  D3,
  input  D4,
  input  D5,
  input  D6,
  input  D7,
  input  T0,
  input  T1,
  input  T2,
  input  T3,
  input  T4,
  input  T5,
  input  T6,
  input  T7,
  input  T8,
  input  T9,
  input  T10,
  input  T11,
  input  T12,
  input  T13,
  input  T14,
  input  T15,
  output AR_Load_Signal,
  output AR_Clear_Signal,
  output SC_Clear_Signal,
  output AC_Load_Signal,
  output AC_Clear_Signal,
  output [2:0] Bus_Select_Lines,
  output PC_Load_Signal,
  output PC_INC_Signal,
  output RAM_Write_Signal,
  output IR_Load_Signal,
  output [3:0] ALU_Signals,
  output DR_Load_Signal
);

  wire AC_out, ADD_2_out, ADD_out, and_1_out, and_2_out, and_3_out, and_4_out, and_5_out, AND_7_out,
       AND_9_out, and_10_out, and_11_out, and_12_out, and_13_out, and_14_out, and_15_out, and_16_out,
       AR_2_out, AR_out, BSA_2_out, BSA_out, BUN_out, CIL_out, CIR_out, CMA_out, DR_2_out, DR_out, INC_out,
       INC_PC_out, INP_out, IR_out, ISZ_1_2_out, ISZ_1_out, ISZ_out, LDA_2_out, LDA_out, not_1_out,
       not_2_out, not_3_out, not_4_out, not_5_out, not_6_out, not_7_out, PC_2_out, PC_out, RAM_2_out,
       RAM_3_out, RAM_4_out, RAM_5_out, RAM_6_out, RAM_out, SNA_out, SPA_out, STA_out, SZA_out, SZE_out;

  not not_1 (not_1_out, T0);
  not not_2 (not_2_out, I);
  and and_1 (and_1_out, D7, T3, not_2_out);
  and and_2 (and_2_out, D7, T3, I);
  not not_3 (not_3_out, D7);
  not not_4 (not_4_out, R);
  and and_3 (and_3_out, not_4_out, T0);
  and and_4 (and_4_out, T2, not_4_out);
  and and_5 (and_5_out, not_3_out, I, T3);
  and and_6 (AR_Clear_Signal, R, R);
  and BUN (BUN_out, D5, T4);
  and BSA (BSA_out, T5, D5);
  and ISZ (ISZ_out, T4, D6);
  and SPA (SPA_out, Operand__0_11[4], and_1_out);
  and SNA (SNA_out, Operand__0_11[3], and_1_out);
  and SZA (SZA_out, Operand__0_11[2], and_1_out);
  and SZE (SZE_out, Operand__0_11[1], and_1_out);
  and INC_PC (INC_PC_out, T1, not_1_out);
  and AND_7 (AND_7_out, D0, T4);
  and ADD (ADD_out, D1, T4);
  and LDA (LDA_out, D2, T4);
  and ISZ_1 (ISZ_1_out, D6, T4);
  and ISZ_1_2 (ISZ_1_2_out, D6, T5);
  or or_1 (AR_Load_Signal, and_3_out, and_4_out, and_5_out);
  or or_2 (DR_Load_Signal, AND_7_out, ADD_out, LDA_out, ISZ_1_out, ISZ_1_2_out);
  or or_3 (PC_Load_Signal, BUN_out, BSA_out, ISZ_out, SPA_out, SNA_out, SZA_out, SZE_out, INC_PC_out);
  or or_4 (PC_INC_Signal, SPA_out, SNA_out, SZA_out, SZE_out, INC_PC_out);
  not not_5 (not_5_out, R);
  and and_8 (IR_Load_Signal, not_5_out, T1);
  and AND_9 (AND_9_out, D0, T5);
  and ADD_2 (ADD_2_out, D1, T5);
  and LDA_2 (LDA_2_out, D2, T5);
  and CMA (CMA_out, Operand__0_11[9], and_1_out);
  and CIR (CIR_out, Operand__0_11[7], and_1_out);
  and CIL (CIL_out, Operand__0_11[6], and_1_out);
  and INP (INP_out, and_2_out, Operand__0_11[11]);
  and INC (INC_out, and_1_out, Operand__0_11[5]);
  and CLR (AC_Clear_Signal, and_1_out, Operand__0_11[11]);
  or or_5 (AC_Load_Signal, AND_9_out, ADD_2_out, LDA_2_out, CMA_out, CIR_out, CIL_out, INP_out, INC_out);
  buf Cin (ALU_Signals[0], INC_out);  // OR_Gate
  buf S0 (ALU_Signals[1], LDA_2_out);  // OR_Gate
  or S1 (ALU_Signals[2], CMA_out, INC_out);
  or S2 (ALU_Signals[3], AND_9_out, LDA_2_out, CMA_out);
  and STA (STA_out, D3, T4);
  and BSA_2 (BSA_2_out, D5, T4);
  and and_10 (and_10_out, D0, T6);
  and and_11 (and_11_out, D1, T6);
  and and_12 (and_12_out, D2, T6);
  and and_13 (and_13_out, D3, T5);
  and and_14 (and_14_out, D4, T5);
  and and_15 (and_15_out, D5, T6);
  and and_16 (and_16_out, D6, T6);
  or or_6 (RAM_Write_Signal, STA_out, BSA_2_out);
  or or_7 (SC_Clear_Signal, and_2_out, and_10_out, and_11_out, and_12_out, and_13_out, and_14_out, AC_Clear_Signal, and_15_out, and_16_out, CMA_out, CIR_out, CIL_out, INC_out);
  not not_6 (not_6_out, D7);
  and RAM (RAM_out, not_6_out, I, T2);
  and RAM_2 (RAM_2_out, D0, T4);
  and RAM_3 (RAM_3_out, D1, T4);
  and RAM_4 (RAM_4_out, D2, T4);
  and RAM_5 (RAM_5_out, D6, T4);
  and AR (AR_out, T4, D4);
  and AR_2 (AR_2_out, D5, T5);
  and PC (PC_out, not_7_out, T0);
  and PC_2 (PC_2_out, T4, D5);
  and DR (DR_out, D2, T5);
  and DR_2 (DR_2_out, D6, T6);
  and AC (AC_out, D3, T4);
  and IR (IR_out, not_7_out, T2);
  and RAM_6 (RAM_6_out, not_7_out, T1);
  not not_7 (not_7_out, R);
  or or_8 (Bus_Select_Lines[0], RAM_5_out, RAM_6_out, RAM_out, RAM_2_out, RAM_3_out, RAM_4_out, AR_out, IR_out, AR_2_out);
  or or_9 (Bus_Select_Lines[1], DR_2_out, DR_out, PC_2_out, PC_out, RAM_5_out, RAM_6_out, RAM_out, RAM_2_out, RAM_3_out, RAM_4_out);
  or or_10 (Bus_Select_Lines[2], DR_2_out, DR_out, RAM_5_out, RAM_6_out, RAM_out, RAM_2_out, RAM_3_out, RAM_4_out, IR_out, AC_out);

  // Notes on the sheet:
  //   r = D7.T3.I'
  //   p = D7.T3.I
  //   AR Control Signals
  //   PC Control Signals
  //   DR Control Signals
  //   IR Control Signals
  //   AC Control Signals
  //   ALU Select Lines and Cin
  //   SC Signals
  //   RAM Write Mode Signal
  //   Bus System Select Lines
endmodule

// DEC
module _16HexSplitter (
  input  [15:0] Input,
  output [3:0] _0,
  output [3:0] _1,
  output [3:0] _2,
  output [3:0] _3
);


  assign _0 = Input[3:0];
  assign _1 = Input[7:4];
  assign _2 = Input[11:8];
  assign _3 = Input[15:12];
endmodule

// DEC
module _12HexSplitter (
  input  [11:0] in_1,
  output [3:0] _0,
  output [3:0] _1,
  output [3:0] _2
);


  assign _0 = in_1[3:0];
  assign _1 = in_1[7:4];
  assign _2 = in_1[11:8];
endmodule

// INC
module _12BitIncrementer (
  input  [11:0] Input,
  output [11:0] Output
);

  Adder #(.width(12)) adder_1 (.a({12{1'b0}}), .b(Input), .out(Output), .cin(1'b1));  // open: cout
endmodule
